// Logisim project Pavlov_code.circ as structural Verilog: 7 circuits, main circuit Из прямого в обратный
module \Из_прямого_в_обратный  (
  input  a,
  input  b,
  input  c,
  input  d
);

  wire decoder_1_out0, decoder_1_out1, decoder_1_out2, decoder_1_out3, decoder_1_out4, decoder_1_out5,
       decoder_1_out6, decoder_1_out7, decoder_2_out0, decoder_2_out1, decoder_3_out0, decoder_3_out1,
       decoder_4_out0, decoder_4_out1, decoder_5_out0, decoder_5_out1, decoder_6_out0, decoder_6_out1,
       or_4_out, or_5_out, or_6_out, or_7_out;
  wire [2:0] or_1_out, priority_encoder_1_out, priority_encoder_2_out;
  wire [3:0] bit_extender_1_out, bit_extender_2_out, bit_extender_3_out, bit_extender_4_out;
  wire [6:0] multiplexer_1_out, multiplexer_2_out, multiplexer_3_out, multiplexer_4_out, multiplexer_5_out,
       multiplexer_6_out, multiplexer_7_out, multiplexer_8_out;

  Decoder #(.select(3), .disabled(0), .enable("false")) decoder_1 (
    .out0(decoder_1_out0), .out1(decoder_1_out1), .out2(decoder_1_out2), .out3(decoder_1_out3),
    .out4(decoder_1_out4), .out5(decoder_1_out5), .out6(decoder_1_out6), .out7(decoder_1_out7),
    .sel({b, c, d}));
  Decoder #(.disabled(0), .enable("false")) decoder_2 (.out0(decoder_2_out0), .out1(decoder_2_out1), .sel(a));
  Priority_Encoder #(.disabled(0)) priority_encoder_1 (
    .in0(decoder_1_out0), .in1(decoder_1_out1), .in2(decoder_1_out2), .in3(decoder_1_out3),
    .in4(decoder_1_out4), .in5(decoder_1_out5), .in6(decoder_1_out6), .in7(decoder_1_out7),
    .out(priority_encoder_1_out), .en_in(decoder_2_out0));  // open: gs, en_out
  Priority_Encoder #(.disabled(0)) priority_encoder_2 (
    .in0(decoder_1_out7), .in1(decoder_1_out6), .in2(decoder_1_out5), .in3(decoder_1_out4),
    .in4(decoder_1_out3), .in5(decoder_1_out2), .in6(decoder_1_out1), .in7(decoder_1_out0),
    .out(priority_encoder_2_out), .en_in(decoder_2_out1));  // open: gs, en_out
  or or_1 (or_1_out[0], priority_encoder_1_out[0], priority_encoder_2_out[0]);
  or or_2 (or_1_out[1], priority_encoder_1_out[1], priority_encoder_2_out[1]);
  or or_3 (or_1_out[2], priority_encoder_1_out[2], priority_encoder_2_out[2]);
  Decoder #(.disabled(0), .enable("false")) decoder_3 (.out0(decoder_3_out0), .out1(decoder_3_out1), .sel(a));
  Multiplexer #(.width(7), .disabled(0), .enable("false")) multiplexer_1 (
    .in0({7{1'b1}}), .in1({7{1'b0}}), .out(multiplexer_1_out), .sel(a));
  Multiplexer #(.width(7), .disabled(0), .enable("false")) multiplexer_2 (
    .in0(7'b1000001), .in1({7{1'b0}}), .out(multiplexer_2_out), .sel(a));
  _7_Segment_Display u_7_segment_display_1 (
    .f(decoder_4_out0), .a(decoder_4_out0), .b(or_4_out), .e(decoder_4_out0), .d(decoder_4_out0), .c(or_4_out));  // open: g, dp
  _7_Segment_Display u_7_segment_display_2 (
    .f(decoder_3_out0), .a(decoder_3_out0), .b(or_5_out), .e(decoder_3_out0), .d(decoder_3_out0),
    .c(or_5_out), .dp(or_5_out));  // open: g
  or or_4 (or_4_out, decoder_4_out0, decoder_4_out1);
  or or_5 (or_5_out, decoder_3_out0, decoder_3_out1);
  Decoder #(.disabled(0), .enable("false")) decoder_4 (.out0(decoder_4_out0), .out1(decoder_4_out1), .sel(or_1_out[2]));
  Multiplexer #(.width(7), .disabled(0), .enable("false")) multiplexer_3 (
    .in0({7{1'b1}}), .in1({7{1'b0}}), .out(multiplexer_3_out), .sel(or_1_out[2]));
  Multiplexer #(.width(7), .disabled(0), .enable("false")) multiplexer_4 (
    .in0(7'b1000001), .in1({7{1'b0}}), .out(multiplexer_4_out), .sel(or_1_out[2]));
  Multiplexer #(.width(7), .disabled(0), .enable("false")) multiplexer_5 (
    .in0({7{1'b1}}), .in1({7{1'b0}}), .out(multiplexer_5_out), .sel(or_1_out[1]));
  Multiplexer #(.width(7), .disabled(0), .enable("false")) multiplexer_6 (
    .in0(7'b1000001), .in1({7{1'b0}}), .out(multiplexer_6_out), .sel(or_1_out[1]));
  _7_Segment_Display u_7_segment_display_3 (
    .f(decoder_5_out0), .a(decoder_5_out0), .b(or_6_out), .e(decoder_5_out0), .d(decoder_5_out0), .c(or_6_out));  // open: g, dp
  or or_6 (or_6_out, decoder_5_out0, decoder_5_out1);
  Decoder #(.disabled(0), .enable("false")) decoder_5 (.out0(decoder_5_out0), .out1(decoder_5_out1), .sel(or_1_out[1]));
  assign bit_extender_1_out = {{3{1'b0}}, a};  // Bit_Extender bit_extender_1
  assign bit_extender_2_out = {{3{1'b0}}, or_1_out[2]};  // Bit_Extender bit_extender_2
  assign bit_extender_3_out = {{3{1'b0}}, or_1_out[1]};  // Bit_Extender bit_extender_3
  assign bit_extender_4_out = {{3{1'b0}}, or_1_out[0]};  // Bit_Extender bit_extender_4
  Multiplexer #(.width(7), .disabled(0), .enable("false")) multiplexer_7 (
    .in0({7{1'b1}}), .in1({7{1'b0}}), .out(multiplexer_7_out), .sel(or_1_out[0]));
  Multiplexer #(.width(7), .disabled(0), .enable("false")) multiplexer_8 (
    .in0(7'b1000001), .in1({7{1'b0}}), .out(multiplexer_8_out), .sel(or_1_out[0]));
  _7_Segment_Display u_7_segment_display_4 (
    .f(decoder_6_out0), .a(decoder_6_out0), .b(or_7_out), .e(decoder_6_out0), .d(decoder_6_out0), .c(or_7_out));  // open: g, dp
  or or_7 (or_7_out, decoder_6_out0, decoder_6_out1);
  Decoder #(.disabled(0), .enable("false")) decoder_6 (.out0(decoder_6_out0), .out1(decoder_6_out1), .sel(or_1_out[0]));
  DotMatrix #(.matrixcols(25)) dotmatrix_1 (
    .col0(multiplexer_1_out), .col1(multiplexer_2_out), .col2(multiplexer_2_out), .col3(multiplexer_2_out),
    .col4({7{1'b1}}), .col5({7{1'b0}}), .col6(7'b0000001), .col7({7{1'b0}}), .col8(multiplexer_3_out),
    .col9(multiplexer_4_out), .col10(multiplexer_4_out), .col11(multiplexer_4_out), .col12({7{1'b1}}),
    .col13({7{1'b0}}), .col14(multiplexer_5_out), .col15(multiplexer_6_out), .col16(multiplexer_6_out),
    .col17(multiplexer_6_out), .col18({7{1'b1}}), .col19({7{1'b0}}), .col20(multiplexer_7_out),
    .col21(multiplexer_8_out), .col22(multiplexer_8_out), .col23(multiplexer_8_out), .col24({7{1'b1}}));
  Hex_Digit_Display hex_digit_display_1 (.value(bit_extender_1_out), .dp(1'b1));
  Hex_Digit_Display hex_digit_display_2 (.value(bit_extender_2_out));  // open: dp
  Hex_Digit_Display hex_digit_display_3 (.value(bit_extender_3_out));  // open: dp
  Hex_Digit_Display hex_digit_display_4 (.value(bit_extender_4_out));  // open: dp

  // Notes on the sheet:
  //   Прямой код
  //   Обратный код
  //   Обратный код
  //   Обратный код
endmodule

module \Вывод_7_или_16  (
  input  in_1,
  input  in_2,
  input  in_3,
  input  in_4
);

  wire decoder_1_out0, decoder_1_out1, decoder_1_out2, decoder_1_out3, decoder_1_out4, decoder_1_out5,
       decoder_1_out6, decoder_1_out7, decoder_1_out8, decoder_1_out9, decoder_1_out10, decoder_1_out11,
       decoder_1_out12, decoder_1_out13, decoder_1_out14, decoder_1_out15, or_1_out, or_2_out, or_3_out,
       or_4_out, or_5_out, or_6_out, or_7_out;

  Decoder #(.select(4), .disabled(0), .enable("false")) decoder_1 (
    .out0(decoder_1_out0), .out1(decoder_1_out1), .out2(decoder_1_out2), .out3(decoder_1_out3),
    .out4(decoder_1_out4), .out5(decoder_1_out5), .out6(decoder_1_out6), .out7(decoder_1_out7),
    .out8(decoder_1_out8), .out9(decoder_1_out9), .out10(decoder_1_out10), .out11(decoder_1_out11),
    .out12(decoder_1_out12), .out13(decoder_1_out13), .out14(decoder_1_out14), .out15(decoder_1_out15),
    .sel({in_1, in_2, in_3, in_4}));
  Hex_Digit_Display hex_digit_display_1 (.value({in_1, in_2, in_3, in_4}));  // open: dp
  or or_1 (or_1_out, decoder_1_out0, decoder_1_out4, decoder_1_out5, decoder_1_out6, decoder_1_out8, decoder_1_out9, decoder_1_out10, decoder_1_out11, decoder_1_out12, decoder_1_out14, decoder_1_out15);
  or or_2 (or_2_out, decoder_1_out2, decoder_1_out3, decoder_1_out4, decoder_1_out5, decoder_1_out6, decoder_1_out8, decoder_1_out9, decoder_1_out10, decoder_1_out11, decoder_1_out13, decoder_1_out14, decoder_1_out15);
  or or_3 (or_3_out, decoder_1_out0, decoder_1_out2, decoder_1_out6, decoder_1_out8, decoder_1_out10, decoder_1_out11, decoder_1_out12, decoder_1_out13, decoder_1_out14, decoder_1_out15);
  _7_Segment_Display u_7_segment_display_1 (
    .g(or_2_out), .f(or_1_out), .a(or_7_out), .b(or_6_out), .e(or_3_out), .d(or_4_out), .c(or_5_out));  // open: dp
  or or_4 (or_4_out, decoder_1_out0, decoder_1_out2, decoder_1_out3, decoder_1_out5, decoder_1_out6, decoder_1_out8, decoder_1_out11, decoder_1_out12, decoder_1_out13, decoder_1_out14);
  or or_5 (or_5_out, decoder_1_out0, decoder_1_out1, decoder_1_out3, decoder_1_out4, decoder_1_out5, decoder_1_out6, decoder_1_out7, decoder_1_out8, decoder_1_out9, decoder_1_out10, decoder_1_out11, decoder_1_out13);
  or or_6 (or_6_out, decoder_1_out0, decoder_1_out1, decoder_1_out2, decoder_1_out3, decoder_1_out4, decoder_1_out7, decoder_1_out8, decoder_1_out9, decoder_1_out10, decoder_1_out13);
  or or_7 (or_7_out, decoder_1_out0, decoder_1_out2, decoder_1_out3, decoder_1_out5, decoder_1_out6, decoder_1_out7, decoder_1_out8, decoder_1_out9, decoder_1_out10, decoder_1_out12, decoder_1_out14, decoder_1_out15);
endmodule

module input_output (
  input  in_1,
  input  in_2,
  output [6:0] out_3
);

  wire clock_1_out, keyboard_1_avail;

  Clock clock_1 (.out(clock_1_out));
  Keyboard keyboard_1 (.clk(clock_1_out), .re(1'b1), .clr(in_1), .avail(keyboard_1_avail), .data(out_3));
  TTY #(.rows(20)) tty_1 (.data(out_3), .clk(clock_1_out), .we(1'b1), .clr(in_2));
endmodule

module \Тест_джойстика  (
);

  wire [4:0] x, y;
  wire [30:0] _1, _2, _3, _4, _5, _6, _7, _8, _9, _10, _11, _12, _13, _14, _15, _16, _17, _18, _19, _20, _21,
       _22, _23, _24, _25, _26, _27, _28, _29, _30, _31, decoder_1_out31;

  DotMatrix #(.matrixcols(31), .matrixrows(31)) dotmatrix_1 (
    .col0(_1), .col1(_2), .col2(_3), .col3(_4), .col4(_5), .col5(_6), .col6(_7), .col7(_8), .col8(_9),
    .col9(_10), .col10(_11), .col11(_12), .col12(_13), .col13(_14), .col14(_15), .col15(_16), .col16(_17),
    .col17(_18), .col18(_19), .col19(_20), .col20(_21), .col21(_22), .col22(_23), .col23(_24), .col24(_25),
    .col25(_26), .col26(_27), .col27(_28), .col28(_29), .col29(_30), .col30(_31));
  Joystick #(.bits(5)) joystick_1 (.x(x), .y(y));
  Decoder #(.select(5), .disabled(0), .enable("false")) decoder_1 (
    .out1(decoder_1_out31[30]), .out2(decoder_1_out31[29]), .out3(decoder_1_out31[28]),
    .out4(decoder_1_out31[27]), .out5(decoder_1_out31[26]), .out6(decoder_1_out31[25]),
    .out7(decoder_1_out31[24]), .out8(decoder_1_out31[23]), .out9(decoder_1_out31[22]),
    .out10(decoder_1_out31[21]), .out11(decoder_1_out31[20]), .out12(decoder_1_out31[19]),
    .out13(decoder_1_out31[18]), .out14(decoder_1_out31[17]), .out15(decoder_1_out31[16]),
    .out16(decoder_1_out31[15]), .out17(decoder_1_out31[14]), .out18(decoder_1_out31[13]),
    .out19(decoder_1_out31[12]), .out20(decoder_1_out31[11]), .out21(decoder_1_out31[10]),
    .out22(decoder_1_out31[9]), .out23(decoder_1_out31[8]), .out24(decoder_1_out31[7]),
    .out25(decoder_1_out31[6]), .out26(decoder_1_out31[5]), .out27(decoder_1_out31[4]),
    .out28(decoder_1_out31[3]), .out29(decoder_1_out31[2]), .out30(decoder_1_out31[1]),
    .out31(decoder_1_out31[0]), .sel(y));  // open: out0
  Demultiplexer #(.select(5), .width(31), .disabled(0), .enable("false")) demultiplexer_1 (
    .out1(_1), .out2(_2), .out3(_3), .out4(_4), .out5(_5), .out6(_6), .out7(_7), .out8(_8), .out9(_9),
    .out10(_10), .out11(_11), .out12(_12), .out13(_13), .out14(_14), .out15(_15), .out16(_16), .out17(_17),
    .out18(_18), .out19(_19), .out20(_20), .out21(_21), .out22(_22), .out23(_23), .out24(_24), .out25(_25),
    .out26(_26), .out27(_27), .out28(_28), .out29(_29), .out30(_30), .out31(_31), .in(decoder_1_out31),
    .sel(x));  // open: out0
endmodule

module \Змейка  (
);

  wire clock_1_out, clock_2_out, reset;
  wire [1:0] x, y;
  wire [3:0] bit_extender_1_out, bit_extender_2_out;
  wire [4:0] adder_1_out, multiplexer_3_out, multiplexer_4_out, register_2_q, subtractor_1_out;
  wire [31:0] _0, _1, _2, _3, _4, _5, _6, _7, _8, _9, _10, _11, _12, _13, _14, _15, _16, _17, _18, _19, _20,
       _21, _22, _23, _24, _25, _26, _27, _28, _29, _30, _31, multiplexer_1_out, multiplexer_2_out,
       register_1_q, shifter_1_out, shifter_2_out;

  DotMatrix #(.matrixcols(32), .matrixrows(32), .persist(10)) dotmatrix_1 (
    .col0(_0), .col1(_1), .col2(_2), .col3(_3), .col4(_4), .col5(_5), .col6(_6), .col7(_7), .col8(_8),
    .col9(_9), .col10(_10), .col11(_11), .col12(_12), .col13(_13), .col14(_14), .col15(_15), .col16(_16),
    .col17(_17), .col18(_18), .col19(_19), .col20(_20), .col21(_21), .col22(_22), .col23(_23), .col24(_24),
    .col25(_25), .col26(_26), .col27(_27), .col28(_28), .col29(_29), .col30(_30), .col31(_31));
  Joystick #(.bits(2)) joystick_1 (.x(x), .y(y));
  Button button_1 (.out(reset));
  Shifter #(.width(32), .shift("rl")) shifter_1 (.in(register_1_q), .\dist (5'b00001), .out(shifter_1_out));
  Shifter #(.width(32), .shift("rr")) shifter_2 (.in(register_1_q), .\dist (5'b00001), .out(shifter_2_out));
  Subtractor #(.width(5)) subtractor_1 (.a(register_2_q), .b(5'b00001), .out(subtractor_1_out));  // open: bin, bout
  Adder #(.width(5)) adder_1 (.a(register_2_q), .b(5'b00001), .out(adder_1_out));  // open: cin, cout
  Multiplexer #(.select(2), .width(32), .disabled(0), .enable("false")) multiplexer_1 (
    .in1(shifter_1_out), .in2(register_1_q), .in3(shifter_2_out), .out(multiplexer_1_out), .sel(y));  // open: in0
  Multiplexer #(.width(32), .disabled(0), .enable("false")) multiplexer_2 (
    .in0(multiplexer_1_out), .in1(32'h10000), .out(multiplexer_2_out), .sel(reset));
  Multiplexer #(.select(2), .width(5), .disabled(0), .enable("false")) multiplexer_3 (
    .in1(subtractor_1_out), .in2(register_2_q), .in3(adder_1_out), .out(multiplexer_3_out), .sel(x));  // open: in0
  Multiplexer #(.width(5), .disabled(0), .enable("false")) multiplexer_4 (
    .in0(multiplexer_3_out), .in1(5'b10000), .out(multiplexer_4_out), .sel(reset));
  Register #(.width(32)) register_1 (
    .D(multiplexer_2_out), .en(1'b1), .Q(register_1_q), .clk(clock_1_out));  // open: clr
  Clock clock_1 (.out(clock_1_out));
  Register #(.width(5)) register_2 (
    .D(multiplexer_4_out), .en(1'b1), .Q(register_2_q), .clk(clock_2_out));  // open: clr
  Clock clock_2 (.out(clock_2_out));
  Demultiplexer #(.select(5), .width(32), .disabled(0), .enable("false")) demultiplexer_1 (
    .out0(_0), .out1(_1), .out2(_2), .out3(_3), .out4(_4), .out5(_5), .out6(_6), .out7(_7), .out8(_8),
    .out9(_9), .out10(_10), .out11(_11), .out12(_12), .out13(_13), .out14(_14), .out15(_15), .out16(_16),
    .out17(_17), .out18(_18), .out19(_19), .out20(_20), .out21(_21), .out22(_22), .out23(_23), .out24(_24),
    .out25(_25), .out26(_26), .out27(_27), .out28(_28), .out29(_29), .out30(_30), .out31(_31),
    .in(register_1_q), .sel(register_2_q));
  assign bit_extender_1_out = {{2{1'b0}}, x};  // Bit_Extender bit_extender_1
  Hex_Digit_Display hex_digit_display_1 (.value(bit_extender_1_out));  // open: dp
  assign bit_extender_2_out = {{2{1'b0}}, y};  // Bit_Extender bit_extender_2
  Hex_Digit_Display hex_digit_display_2 (.value(bit_extender_2_out));  // open: dp
endmodule

module flappy_bird (
  input  [4:0] in_1,
  input  in_2,
  input  in_3,
  input  in_4,
  input  in_5
);

  wire and_1_out, and_2_out, and_3_out, and_4_out, and_5_out, and_6_out, and_7_out, and_8_out, and_9_out,
       and_10_out, and_11_out, and_12_out, and_13_out, and_14_out, and_15_out, and_16_out, and_17_out,
       and_18_out, and_19_out, and_20_out, and_21_out, and_22_out, and_23_out, and_24_out, and_25_out,
       and_26_out, and_27_out, and_28_out, and_29_out, and_30_out, and_31_out, and_32_out, clock_1_out,
       clock_2_out, comparator_2_eq, comparator_3_eq, jump, or_1_out, or_2_out, or_3_out, reset, restart,
       stop;
  wire [1:0] counter, priority_encoder_1_out;
  wire [4:0] adder_1_out, multiplexer_4_out, multiplexer_5_out, now, subtractor_1_out;
  wire [31:0] _0, _01, _1, _1_5, _1_6, _1_7, _1_8, _1_9, _1_10, _1_11, _1_12, _1_13, _1_14, _1_15, _1_16,
       _1_17, _1_18, _1_19, _1_20, _1_21, _1_22, _1_23, _1_24, _1_25, _1_26, _2, _3, _4, _5, _6, _7, _8, _9,
       _10, _11, _12, _13, _14, _15, _16, _17, _18, _19, _20, _21, _22, _23, _24, _25, _26, _27, _28, _29,
       _30, _31, multiplexer_1_out, multiplexer_2_out, multiplexer_3_out, rom_1_data, rom_2_data, rom_3_data,
       rom_4_data, shifter_1_out, shifter_2_out;

  DotMatrix #(.matrixcols(32), .matrixrows(32)) dotmatrix_1 (
    .col0(_0), .col1(_1), .col2(_2), .col3(_3), .col4(_4), .col5(_5), .col6(_6), .col7(_7), .col8(_8),
    .col9(_9), .col10(_10), .col11(_11), .col12(_12), .col13(_13), .col14(_14), .col15(_15), .col16(_16),
    .col17(_17), .col18(_18), .col19(_19), .col20(_20), .col21(_21), .col22(_22), .col23(_23), .col24(_24),
    .col25(_25), .col26(_26), .col27(_27), .col28(_28), .col29(_29), .col30(_30), .col31(_31));
  Button button_1 (.out(jump));
  Button button_2 (.out(restart));
  Shifter #(.width(32), .shift("rr")) shifter_1 (.in(_0), .\dist (5'b00001), .out(shifter_1_out));
  Shifter #(.width(32), .shift("rl")) shifter_2 (.in(_0), .\dist (5'b00001), .out(shifter_2_out));
  Multiplexer #(.width(32), .disabled(0), .enable("false")) multiplexer_1 (
    .in0(shifter_1_out), .in1(32'h8000), .out(multiplexer_1_out), .sel(restart));
  Multiplexer #(.width(32), .disabled(0), .enable("false")) multiplexer_2 (
    .in0(multiplexer_1_out), .in1(shifter_2_out), .out(multiplexer_2_out), .sel(jump));
  Clock clock_1 (.out(clock_1_out));
  Register #(.width(32)) register_1 (.D(multiplexer_2_out), .en(1'b1), .Q(_0), .clk(clock_1_out), .clr(stop));
  and and_1 (and_1_out, _0[1], _01[1]);
  and and_2 (and_2_out, _0[0], _01[0]);
  and and_3 (and_3_out, _0[2], _01[2]);
  and and_4 (and_4_out, _0[29], _01[29]);
  and and_5 (and_5_out, _0[30], _01[30]);
  and and_6 (and_6_out, _0[31], _01[31]);
  and and_7 (and_7_out, _0[5], _01[5]);
  and and_8 (and_8_out, _0[3], _01[3]);
  and and_9 (and_9_out, _0[4], _01[4]);
  and and_10 (and_10_out, _0[27], _01[27]);
  and and_11 (and_11_out, _0[26], _01[26]);
  and and_12 (and_12_out, _0[28], _01[28]);
  and and_13 (and_13_out, _0[7], _01[7]);
  and and_14 (and_14_out, _0[6], _01[6]);
  and and_15 (and_15_out, _0[24], _01[24]);
  and and_16 (and_16_out, _0[25], _01[25]);
  ROM #(.addrWidth(2), .dataWidth(32)) rom_1 (.addr(counter), .data(rom_1_data), .sel(in_2));
  ROM #(.addrWidth(2), .dataWidth(32)) rom_2 (.addr(counter), .data(rom_2_data), .sel(in_3));
  ROM #(.addrWidth(2), .dataWidth(32)) rom_3 (.addr(counter), .data(rom_3_data), .sel(in_4));
  ROM #(.addrWidth(2), .dataWidth(32)) rom_4 (.addr(counter), .data(rom_4_data), .sel(in_5));
  and and_17 (and_17_out, _0[8], _01[8]);
  and and_18 (and_18_out, _0[10], _01[10]);
  and and_19 (and_19_out, _0[9], _01[9]);
  and and_20 (and_20_out, _0[21], _01[21]);
  and and_21 (and_21_out, _0[22], _01[22]);
  and and_22 (and_22_out, _0[23], _01[23]);
  Priority_Encoder #(.select(2), .disabled(0)) priority_encoder_1 (
    .in0(in_2), .in1(in_3), .in2(in_4), .in3(in_5), .out(priority_encoder_1_out));  // open: gs, en_out, en_in
  and and_23 (and_23_out, _0[12], _01[12]);
  and and_24 (and_24_out, _0[11], _01[11]);
  and and_25 (and_25_out, _0[13], _01[13]);
  and and_26 (and_26_out, _0[18], _01[18]);
  and and_27 (and_27_out, _0[19], _01[19]);
  and and_28 (and_28_out, _0[20], _01[20]);
  Multiplexer #(.select(2), .width(32), .disabled(0), .enable("false")) multiplexer_3 (
    .in0(rom_1_data), .in1(rom_2_data), .in2(rom_3_data), .in3(rom_4_data), .out(multiplexer_3_out),
    .sel(priority_encoder_1_out));
  and and_29 (and_29_out, _0[14], _01[14]);
  and and_30 (and_30_out, _0[15], _01[15]);
  and and_31 (and_31_out, _0[17], _01[17]);
  and and_32 (and_32_out, _0[16], _01[16]);
  Comparator #(.width(5), .mode("unsigned")) comparator_1 (.a(now), .b(in_1), .eq(reset));  // open: gt, lt
  Subtractor #(.width(5)) subtractor_1 (.a(now), .b(5'b00001), .out(subtractor_1_out));  // open: bin, bout
  Multiplexer #(.width(5), .disabled(0), .enable("false")) multiplexer_4 (
    .in0(subtractor_1_out), .in1({5{1'b1}}), .out(multiplexer_4_out), .sel(or_1_out));
  or or_1 (or_1_out, reset, restart);
  Counter #(.width(2), .max('h3), .trigger("falling")) counter_1 (
    .Q(counter), .clk(reset), .clr(restart));  // open: load, D, count, carry
  Register #(.width(5)) register_2 (.D(multiplexer_4_out), .en(1'b1), .Q(now), .clk(clock_2_out), .clr(stop));
  Clock clock_2 (.out(clock_2_out));
  Demultiplexer #(.select(5), .width(32), .disabled(0), .enable("false")) demultiplexer_1 (
    .out0(_01), .out1(_1), .out2(_2), .out3(_3), .out4(_4), .out5(_1_5), .out6(_1_6), .out7(_1_7),
    .out8(_1_8), .out9(_1_9), .out10(_1_10), .out11(_1_11), .out12(_1_12), .out13(_1_13), .out14(_1_14),
    .out15(_1_15), .out16(_1_16), .out17(_1_17), .out18(_1_18), .out19(_1_19), .out20(_1_20), .out21(_1_21),
    .out22(_1_22), .out23(_1_23), .out24(_1_24), .out25(_1_25), .out26(_1_26), .out27(_27), .out28(_28),
    .out29(_29), .out30(_30), .out31(_31), .in(multiplexer_3_out), .sel(now));
  or or_2 (or_2_out, and_2_out, and_1_out, and_3_out, and_8_out, and_9_out, and_7_out, and_14_out, and_13_out, and_17_out, and_19_out, and_18_out, and_24_out, and_23_out, and_25_out, and_29_out, and_30_out, and_32_out, and_31_out, and_26_out, and_27_out, and_28_out, and_20_out, and_21_out, and_22_out, and_15_out, and_16_out, and_11_out, and_10_out, and_12_out, and_4_out, and_5_out, and_6_out);
  Demultiplexer #(.select(5), .width(32), .disabled(0), .enable("false")) demultiplexer_2 (
    .out1(_1), .out2(_2), .out3(_3), .out4(_4), .out5(_5), .out6(_6), .out7(_7), .out8(_8), .out9(_9),
    .out10(_10), .out11(_11), .out12(_12), .out13(_13), .out14(_14), .out15(_15), .out16(_16), .out17(_17),
    .out18(_18), .out19(_19), .out20(_20), .out21(_21), .out22(_22), .out23(_23), .out24(_24), .out25(_25),
    .out26(_26), .out27(_27), .out28(_28), .out29(_29), .out30(_30), .out31(_31), .in(multiplexer_3_out),
    .sel(multiplexer_5_out));  // open: out0
  Adder #(.width(5)) adder_1 (.a(now), .b(5'b00001), .out(adder_1_out));  // open: cin, cout
  Multiplexer #(.width(5), .disabled(0), .enable("false")) multiplexer_5 (
    .in0(adder_1_out), .in1(now), .out(multiplexer_5_out), .sel(stop));
  Comparator #(.width(32), .mode("unsigned")) comparator_2 (
    .a(_0), .b(32'h80000000), .eq(comparator_2_eq));  // open: gt, lt
  Comparator #(.width(32), .mode("unsigned")) comparator_3 (.a(_0), .b(32'h1), .eq(comparator_3_eq));  // open: gt, lt
  or or_3 (or_3_out, comparator_2_eq, or_2_out, comparator_3_eq);
  T_Flip_Flop t_ff_1 (.clk(or_3_out), .T(1'b1), .Q(stop), .reset(restart), .en(1'b1));  // open: Qn, preset
  Multiplexer #(.width(32), .disabled(0), .enable("false")) multiplexer_6 (
    .in0(_1_5), .in1(32'h1f0), .out(_5), .sel(stop));
  Multiplexer #(.width(32), .disabled(0), .enable("false")) multiplexer_7 (
    .in0(_1_6), .in1(32'h3e0140), .out(_6), .sel(stop));
  Multiplexer #(.width(32), .disabled(0), .enable("false")) multiplexer_8 (
    .in0(_1_7), .in1(32'hfa201f0), .out(_7), .sel(stop));
  Multiplexer #(.width(32), .disabled(0), .enable("false")) multiplexer_9 (
    .in0(_1_8), .in1(32'h8a24000), .out(_8), .sel(stop));
  Multiplexer #(.width(32), .disabled(0), .enable("false")) multiplexer_10 (
    .in0(_1_9), .in1(32'habe41f0), .out(_9), .sel(stop));
  Multiplexer #(.width(32), .disabled(0), .enable("false")) multiplexer_11 (
    .in0(_1_10), .in1(32'hb807d10), .out(_10), .sel(stop));
  Multiplexer #(.width(32), .disabled(0), .enable("false")) multiplexer_12 (
    .in0(_1_11), .in1(32'h384150), .out(_11), .sel(stop));
  Multiplexer #(.width(32), .disabled(0), .enable("false")) multiplexer_13 (
    .in0(_1_12), .in1(32'hf844170), .out(_12), .sel(stop));
  Multiplexer #(.width(32), .disabled(0), .enable("false")) multiplexer_14 (
    .in0(_1_13), .in1(32'ha020000), .out(_13), .sel(stop));
  Multiplexer #(.width(32), .disabled(0), .enable("false")) multiplexer_15 (
    .in0(_1_14), .in1(32'hf847df0), .out(_14), .sel(stop));
  Multiplexer #(.width(32), .disabled(0), .enable("false")) multiplexer_16 (
    .in0(_1_15), .in1(32'h385140), .out(_15), .sel(stop));
  Multiplexer #(.width(32), .disabled(0), .enable("false")) multiplexer_17 (
    .in0(_1_16), .in1(32'hf8059f0), .out(_16), .sel(stop));
  Multiplexer #(.width(32), .disabled(0), .enable("false")) multiplexer_18 (
    .in0(_1_17), .in1(32'h43e7400), .out(_17), .sel(stop));
  Multiplexer #(.width(32), .disabled(0), .enable("false")) multiplexer_19 (
    .in0(_1_18), .in1(32'h22a0110), .out(_18), .sel(stop));
  Multiplexer #(.width(32), .disabled(0), .enable("false")) multiplexer_20 (
    .in0(_1_19), .in1(32'h42a41f0), .out(_19), .sel(stop));
  Multiplexer #(.width(32), .disabled(0), .enable("false")) multiplexer_21 (
    .in0(_1_20), .in1(32'hf802110), .out(_20), .sel(stop));
  Multiplexer #(.width(32), .disabled(0), .enable("false")) multiplexer_22 (
    .in0(_1_21), .in1(32'h3e1c00), .out(_21), .sel(stop));
  Multiplexer #(.width(32), .disabled(0), .enable("false")) multiplexer_23 (
    .in0(_1_22), .in1(32'hfa821f0), .out(_22), .sel(stop));
  Multiplexer #(.width(32), .disabled(0), .enable("false")) multiplexer_24 (
    .in0(_1_23), .in1(32'haac4080), .out(_23), .sel(stop));
  Multiplexer #(.width(32), .disabled(0), .enable("false")) multiplexer_25 (
    .in0(_1_24), .in1(32'haba0040), .out(_24), .sel(stop));
  Multiplexer #(.width(32), .disabled(0), .enable("false")) multiplexer_26 (
    .in0(_1_25), .in1(32'h20), .out(_25), .sel(stop));
  Multiplexer #(.width(32), .disabled(0), .enable("false")) multiplexer_27 (
    .in0(_1_26), .in1(32'h1f0), .out(_26), .sel(stop));

  // Other names for the same wires on the sheet: level_1 = in_2; level_2 = in_3; level_3 = in_4; level_4 = in_5

  // Notes on the sheet:
  //   contents of rom_1 (hex, n*v repeats v):
  //   c0000003 f000000f fc00003f ff0000ff
  //   contents of rom_2 (hex, n*v repeats v):
  //   ff000fff f000ffff ffff000f f000ffff
  //   contents of rom_3 (hex, n*v repeats v):
  //   ff0000ff f001800f fff00fff f00ff00f
  //   contents of rom_4 (hex, n*v repeats v):
  //   ffff0fff ff0fffff ffffff0f c3ffffff
endmodule

module \Универсальный_счетчик  (
  input  in_1,
  input  in_2,
  input  in_3,
  input  in_4,
  input  in_5,
  input  in_6,
  input  in_7,
  input  in_8,
  input  in_9,
  input  in_10
);

  wire and_1_out, and_2_out, and_3_out, and_4_out, clock_1_out, clock_2_out, clock_3_out, clock_4_out,
       d_ff_1_qn, d_ff_2_qn, d_ff_3_qn, d_ff_4_qn, d_ff_5_qn, or_1_out, or_2_out, or_3_out, or_4_out,
       xnor_1_out, xnor_2_out, xnor_3_out, xnor_4_out, xnor_5_out, xnor_6_out, xnor_7_out, xnor_8_out,
       xnor_9_out, xnor_10_out, \сброс_2_out , \сброс_3_out , \сброс_4_out , \сброс_out ;
  wire [1:0] d_ff_1_q, t_ff_1_q;
  wire [2:0] d_ff_3_q, t_ff_3_q;
  wire [3:0] bit_extender_1_out, bit_extender_2_out, bit_extender_3_out, bit_extender_4_out,
       multiplexer_1_out, multiplexer_2_out, multiplexer_3_out, multiplexer_4_out, undriven, undriven_2,
       undriven_3, undriven_4, undriven_5, undriven_6, undriven_7, undriven_8, undriven_9, undriven_10,
       undriven_11, undriven_12, undriven_13, undriven_14, undriven_15, undriven_16, undriven_17,
       undriven_18, undriven_19, undriven_20, undriven_21, undriven_22, undriven_23, undriven_24;

  Clock clock_1 (.out(clock_1_out));
  Button \u_сброс  (.out(\сброс_out ));
  Clock clock_2 (.out(clock_2_out));
  Button \u_сброс_2  (.out(\сброс_2_out ));
  or or_1 (or_1_out, \сброс_2_out , and_2_out);
  D_Flip_Flop d_ff_1 (
    .clk(clock_1_out), .D(d_ff_1_qn), .Q(d_ff_1_q[0]), .Qn(d_ff_1_qn), .preset(1'b0), .en(1'b1),
    .reset(or_2_out));
  or or_2 (or_2_out, \сброс_out , and_1_out);
  T_Flip_Flop #(.trigger("falling")) t_ff_1 (
    .clk(clock_2_out), .T(1'b1), .Q(t_ff_1_q[0]), .preset(1'b0), .reset(or_1_out), .en(1'b1));  // open: Qn
  T_Flip_Flop #(.trigger("falling")) t_ff_2 (
    .clk(t_ff_1_q[0]), .T(1'b1), .Q(t_ff_1_q[1]), .preset(1'b0), .reset(or_1_out), .en(1'b1));  // open: Qn
  D_Flip_Flop d_ff_2 (
    .clk(d_ff_1_qn), .D(d_ff_2_qn), .Q(d_ff_1_q[1]), .Qn(d_ff_2_qn), .preset(1'b0), .en(1'b1),
    .reset(or_2_out));
  xnor xnor_1 (xnor_1_out, in_2, t_ff_1_q[1]);
  xnor xnor_2 (xnor_2_out, in_4, t_ff_1_q[0]);
  xnor xnor_3 (xnor_3_out, in_7, d_ff_1_q[1]);
  xnor xnor_4 (xnor_4_out, in_9, d_ff_1_q[0]);
  Hex_Digit_Display hex_digit_display_1 (.value(bit_extender_1_out));  // open: dp
  assign bit_extender_1_out = {{2{1'b0}}, t_ff_1_q};  // Bit_Extender bit_extender_1
  and and_1 (and_1_out, xnor_3_out, xnor_4_out, clock_1_out);
  Hex_Digit_Display hex_digit_display_2 (.value(bit_extender_2_out));  // open: dp
  assign bit_extender_2_out = {{2{1'b0}}, d_ff_1_q};  // Bit_Extender bit_extender_2
  Multiplexer #(.select(2), .width(4), .disabled(0), .enable("false")) multiplexer_1 (
    .in0(undriven_5), .in1(undriven_6), .in2(undriven_7), .in3(undriven_8), .out(multiplexer_1_out),
    .sel(t_ff_1_q));
  and and_2 (and_2_out, xnor_1_out, xnor_2_out, clock_2_out);
  Hex_Digit_Display hex_digit_display_3 (.value(multiplexer_2_out));  // open: dp
  Multiplexer #(.select(2), .width(4), .disabled(0), .enable("false")) multiplexer_2 (
    .in0(undriven), .in1(undriven_2), .in2(undriven_3), .in3(undriven_4), .out(multiplexer_2_out),
    .sel(d_ff_1_q));
  Hex_Digit_Display hex_digit_display_4 (.value(multiplexer_1_out));  // open: dp
  Clock clock_3 (.out(clock_3_out));
  Button \u_сброс_3  (.out(\сброс_3_out ));
  Clock clock_4 (.out(clock_4_out));
  Button \u_сброс_4  (.out(\сброс_4_out ));
  or or_3 (or_3_out, \сброс_4_out , and_3_out);
  D_Flip_Flop d_ff_3 (
    .clk(clock_3_out), .D(d_ff_3_qn), .Q(d_ff_3_q[0]), .Qn(d_ff_3_qn), .preset(1'b0), .en(1'b1),
    .reset(or_4_out));
  or or_4 (or_4_out, \сброс_3_out , and_4_out);
  T_Flip_Flop #(.trigger("falling")) t_ff_3 (
    .clk(clock_4_out), .T(1'b1), .Q(t_ff_3_q[0]), .preset(1'b0), .reset(or_3_out), .en(1'b1));  // open: Qn
  D_Flip_Flop d_ff_4 (
    .clk(d_ff_3_qn), .D(d_ff_4_qn), .Q(d_ff_3_q[1]), .Qn(d_ff_4_qn), .preset(1'b0), .en(1'b1),
    .reset(or_4_out));
  T_Flip_Flop #(.trigger("falling")) t_ff_4 (
    .clk(t_ff_3_q[0]), .T(1'b1), .Q(t_ff_3_q[1]), .preset(1'b0), .reset(or_3_out), .en(1'b1));  // open: Qn
  T_Flip_Flop #(.trigger("falling")) t_ff_5 (
    .clk(t_ff_3_q[1]), .T(1'b1), .Q(t_ff_3_q[2]), .preset(1'b0), .reset(or_3_out), .en(1'b1));  // open: Qn
  D_Flip_Flop d_ff_5 (
    .clk(d_ff_4_qn), .D(d_ff_5_qn), .Q(d_ff_3_q[2]), .Qn(d_ff_5_qn), .preset(1'b0), .en(1'b1),
    .reset(or_4_out));
  xnor xnor_5 (xnor_5_out, in_1, t_ff_3_q[2]);
  xnor xnor_6 (xnor_6_out, in_3, t_ff_3_q[1]);
  xnor xnor_7 (xnor_7_out, in_5, t_ff_3_q[0]);
  xnor xnor_8 (xnor_8_out, in_6, d_ff_3_q[2]);
  xnor xnor_9 (xnor_9_out, in_8, d_ff_3_q[1]);
  xnor xnor_10 (xnor_10_out, in_10, d_ff_3_q[0]);
  and and_3 (and_3_out, xnor_5_out, xnor_6_out, xnor_7_out, clock_4_out);
  Hex_Digit_Display hex_digit_display_5 (.value(bit_extender_3_out));  // open: dp
  assign bit_extender_3_out = {{1{1'b0}}, t_ff_3_q};  // Bit_Extender bit_extender_3
  and and_4 (and_4_out, xnor_8_out, xnor_9_out, xnor_10_out, clock_3_out);
  Hex_Digit_Display hex_digit_display_6 (.value(bit_extender_4_out));  // open: dp
  assign bit_extender_4_out = {{1{1'b0}}, d_ff_3_q};  // Bit_Extender bit_extender_4
  Multiplexer #(.select(3), .width(4), .disabled(0), .enable("false")) multiplexer_3 (
    .in0(undriven_9), .in1(undriven_10), .in2(undriven_11), .in3(undriven_12), .in4(undriven_13),
    .in5(undriven_14), .in6(undriven_15), .in7(undriven_16), .out(multiplexer_3_out), .sel(t_ff_3_q));
  Multiplexer #(.select(3), .width(4), .disabled(0), .enable("false")) multiplexer_4 (
    .in0(undriven_17), .in1(undriven_18), .in2(undriven_19), .in3(undriven_20), .in4(undriven_21),
    .in5(undriven_22), .in6(undriven_23), .in7(undriven_24), .out(multiplexer_4_out), .sel(d_ff_3_q));
  Hex_Digit_Display hex_digit_display_7 (.value(multiplexer_3_out));  // open: dp
  Hex_Digit_Display hex_digit_display_8 (.value(multiplexer_4_out));  // open: dp
endmodule
