// Logisim project Pavlov_triggers.circ as structural Verilog: 1 circuit, main circuit main
module main (
  input  not_S,
  input  not_R,
  input  R,
  input  S,
  input  S_2,
  input  C,
  input  R_2,
  input  not_S_2,
  input  S_3,
  input  C_2,
  input  R_3,
  input  not_R_2,
  input  D,
  input  C_3,
  input  not_S_3,
  input  not_R_3,
  input  not_S_4,
  input  not_R_4,
  input  not_S_5,
  input  T,
  input  not_R_5,
  input  not_S_6,
  input  J,
  input  C_4,
  input  K,
  input  not_R_6
);

  wire C_2_out, C_out, nand_1_out, nand_2_out, nand_3_out, nand_4_out, nand_5_out, nand_6_out, nand_7_out,
       nand_8_out, nand_9_out, nand_10_out, nand_11_out, nand_12_out, nand_13_out, nand_14_out, nand_15_out,
       nand_16_out, nand_17_out, nand_18_out, nand_19_out, nand_20_out, nand_21_out, nand_22_out,
       nand_23_out, nand_24_out, nand_25_out, nand_26_out, nand_27_out, nand_28_out, nand_29_out,
       nand_30_out, nand_31_out, nand_32_out, nand_33_out, nand_34_out, nand_35_out, nand_36_out,
       nand_37_out, nand_38_out, nand_39_out, nand_40_out, nand_41_out, nand_42_out, nand_43_out, nor_1_out,
       nor_2_out, nor_3_out, nor_4_out, nor_5_out, nor_6_out, nor_7_out, nor_8_out;

  Clock u_C (.out(C_out));
  Clock u_C_2 (.out(C_2_out));
  nand nand_1 (nand_1_out, not_S, nand_2_out);
  nand nand_2 (nand_2_out, nand_1_out, not_R);
  nor nor_1 (nor_1_out, R, nor_2_out);
  nor nor_2 (nor_2_out, nor_1_out, S);
  nand nand_3 (nand_3_out, C_2, C_2);
  nand nand_4 (nand_4_out, D, D);
  nand nand_5 (nand_5_out, not_S_3, nand_16_out);
  nand nand_6 (nand_6_out, nand_17_out, not_R_3);
  nor nor_3 (nor_3_out, not_S_4, nor_5_out);
  nor nor_4 (nor_4_out, nor_6_out, not_R_4);
  nand nand_7 (nand_7_out, T, T);
  nand nand_8 (nand_8_out, nand_39_out, J, C_4);
  nand nand_9 (nand_9_out, C_4, K, nand_38_out);
  LED Q (.in(nand_1_out));
  LED not_Q (.in(nand_2_out));
  LED Q_2 (.in(nor_1_out));
  LED not_Q_2 (.in(nor_2_out));
  nand nand_10 (nand_10_out, S_2, C);
  nand nand_11 (nand_11_out, C, R_2);
  nand nand_12 (nand_12_out, S_3, nand_3_out);
  nand nand_13 (nand_13_out, nand_3_out, R_3);
  nand nand_14 (nand_14_out, D, C_3);
  nand nand_15 (nand_15_out, C_3, nand_4_out);
  nand nand_16 (nand_16_out, nand_17_out, nand_5_out, C_out);
  nand nand_17 (nand_17_out, C_out, nand_6_out, nand_16_out);
  nor nor_5 (nor_5_out, nor_6_out, nor_3_out, C_2_out);
  nor nor_6 (nor_6_out, C_2_out, nor_4_out, nor_5_out);
  nand nand_18 (nand_18_out, nand_43_out, nand_7_out);
  nand nand_19 (nand_19_out, nand_7_out, nand_42_out);
  nand nand_20 (nand_20_out, not_S_6, nand_8_out, nand_21_out);
  nand nand_21 (nand_21_out, nand_20_out, nand_9_out, not_R_6);
  nand nand_22 (nand_22_out, nand_10_out, nand_23_out);
  nand nand_23 (nand_23_out, nand_22_out, nand_11_out);
  nand nand_24 (nand_24_out, not_S_2, nand_12_out, nand_25_out);
  nand nand_25 (nand_25_out, nand_24_out, nand_13_out, not_R_2);
  nand nand_26 (nand_26_out, nand_14_out, nand_27_out);
  nand nand_27 (nand_27_out, nand_26_out, nand_15_out);
  nand nand_28 (nand_28_out, not_S_5, nand_18_out, nand_29_out);
  nand nand_29 (nand_29_out, nand_28_out, nand_19_out, not_R_5);
  nand nand_30 (nand_30_out, nand_20_out, nand_8_out, nand_9_out);
  nand nand_31 (nand_31_out, nand_9_out, nand_8_out, nand_21_out);
  LED Q_3 (.in(nand_22_out));
  LED not_Q_3 (.in(nand_23_out));
  nand nand_32 (nand_32_out, nand_24_out, C_2);
  nand nand_33 (nand_33_out, C_2, nand_25_out);
  LED Q_4 (.in(nand_26_out));
  LED not_Q_4 (.in(nand_27_out));
  nand nand_34 (nand_34_out, nand_16_out, nand_35_out);
  LED Q_5 (.in(nand_34_out));
  LED not_Q_5 (.in(nand_35_out));
  nand nand_35 (nand_35_out, nand_34_out, nand_17_out);
  LED Q_6 (.in(nor_7_out));
  nor nor_7 (nor_7_out, nor_5_out, nor_8_out);
  LED not_Q_6 (.in(nor_8_out));
  nor nor_8 (nor_8_out, nor_7_out, nor_6_out);
  nand nand_36 (nand_36_out, nand_28_out, T);
  nand nand_37 (nand_37_out, T, nand_29_out);
  nand nand_38 (nand_38_out, not_S_6, nand_39_out, nand_30_out);
  LED Q_7 (.in(nand_38_out));
  nand nand_39 (nand_39_out, nand_31_out, nand_38_out, not_R_6);
  LED not_Q_7 (.in(nand_39_out));
  LED Q_8 (.in(nand_40_out));
  nand nand_40 (nand_40_out, not_S_2, nand_32_out, nand_41_out);
  LED not_Q_8 (.in(nand_41_out));
  nand nand_41 (nand_41_out, nand_40_out, nand_33_out, not_R_2);
  nand nand_42 (nand_42_out, not_S_5, nand_36_out, nand_43_out);
  LED Q_9 (.in(nand_42_out));
  nand nand_43 (nand_43_out, nand_42_out, nand_37_out, not_R_5);
  LED not_Q_9 (.in(nand_43_out));
endmodule
